# Fritzing sketch keyboard_numpad (saved by Fritzing 0.9.3b)
circuit board: 8cm x 10cm
breadboards: 1

parts:
  ROW = female pin header, 5 pins [form="♀ (female)"]
  COLUMN = female pin header, 4 pins [form="♀ (female)"]
  S2 = Cherry MX Keyswitch
  S3 = Cherry MX Keyswitch
  S4 = Cherry MX Keyswitch
  S5 = Cherry MX Keyswitch
  S6 = Cherry MX Keyswitch
  S7 = Cherry MX Keyswitch
  S8 = Cherry MX Keyswitch
  S9 = Cherry MX Keyswitch
  S10 = Cherry MX Keyswitch
  S11 = Cherry MX Keyswitch
  S12 = Cherry MX Keyswitch
  S13 = Cherry MX Keyswitch
  S14 = Cherry MX Keyswitch
  S15 = Cherry MX Keyswitch
  S18 = Cherry MX Keyswitch
  S17 = Cherry MX Keyswitch
  D1 = Diode [package=diode-1n4148]
  D2 = Diode [package=diode-1n4148]
  D3 = Diode [package=diode-1n4148]
  D4 = Diode [package=diode-1n4148]
  D5 = Diode [package=diode-1n4148]
  D6 = Diode [package=diode-1n4148]
  D8 = Diode [package=diode-1n4148]
  D7 = Diode [package=diode-1n4148]
  D10 = Diode [package=diode-1n4148]
  D11 = Diode [package=diode-1n4148]
  D10_2 = Diode [package=diode-1n4148]
  D16 = Diode [package=diode-1n4148]
  D14 = Diode [package=diode-1n4148]
  D14_2 = Diode [package=diode-1n4148]
  D15 = Diode [package=diode-1n4148]
  D18 = Diode [package=diode-1n4148]
  D17 = Diode [package=diode-1n4148]
  S1 = Cherry MX Keyswitch
  LED_COL1 = female pin header, 6 pins [form="♀ (female)"]
  LED_COL2 = female pin header, 3 pins [form="♀ (female)"]
  LED_COL3 = female pin header, 3 pins [form="♀ (female)"]
  LED_ROW = female pin header, 5 pins [form="♀ (female)"]

nets:
  N1: ROW.pin1, D1.C, D2.C, D3.C, D4.C
  N2: ROW.pin2, D5.C, D6.C, D8.C, D7.C
  N3: ROW.pin3, D10.C, D11.C, D10_2.C
  N4: ROW.pin4, D16.C, D14.C, D14_2.C, D15.C
  N5: ROW.pin5, D18.C, D17.C
  N6: COLUMN.pin1, S5.pin_2, S11.pin_2, S12.pin_2, S15.pin_2, S1.pin_2
  N7: COLUMN.pin2, S2.pin_2, S6.pin_2, S10.pin_2, S13.pin_2
  N8: COLUMN.pin3, S3.pin_2, S7.pin_2, S9.pin_2, S14.pin_2, S18.pin_2
  N9: COLUMN.pin4, S4.pin_2, S8.pin_2, S17.pin_2
  N10: S2.pin_1, S2.pin_6, S3.pin_1, S3.pin_6, S4.pin_1, S4.pin_6, S5.pin_1, S5.pin_6, S6.pin_1, S6.pin_6, S7.pin_1, S7.pin_6, S8.pin_1, S8.pin_6, S9.pin_1, S9.pin_6, S10.pin_1, S10.pin_6, S11.pin_1, S11.pin_6, S12.pin_1, S12.pin_6, S13.pin_1, S13.pin_6, S14.pin_1, S14.pin_6, S15.pin_1, S15.pin_6, S18.pin_1, S18.pin_6, S17.pin_1, S17.pin_6, S1.pin_1, S1.pin_6, LED_COL1.pin1, LED_COL1.pin4, LED_COL2.pin1, LED_COL3.pin1, LED_ROW.pin1, LED_ROW.pin2, LED_ROW.pin3, LED_ROW.pin4, LED_ROW.pin5
  N11: S2.pin_3, D2.A
  N12: S2.pin_4, S2.pin_5, S6.pin_4, S6.pin_5, S10.pin_4, S10.pin_5, S13.pin_4, S13.pin_5, LED_COL1.pin5, LED_COL1.pin6
  N13: S3.pin_3, D3.A
  N14: S3.pin_4, S3.pin_5, S7.pin_4, S7.pin_5, S9.pin_4, S9.pin_5, S14.pin_4, S14.pin_5, S18.pin_4, S18.pin_5, LED_COL2.pin2, LED_COL2.pin3
  N15: S4.pin_3, D4.A
  N16: S4.pin_4, S4.pin_5, S8.pin_4, S8.pin_5, S17.pin_4, S17.pin_5, LED_COL3.pin2, LED_COL3.pin3
  N17: S5.pin_3, D5.A
  N18: S5.pin_4, S5.pin_5, S11.pin_4, S11.pin_5, S12.pin_4, S12.pin_5, S15.pin_4, S15.pin_5, S1.pin_4, S1.pin_5, LED_COL1.pin2, LED_COL1.pin3
  N19: S6.pin_3, D7.A
  N20: S7.pin_3, D6.A
  N21: S8.pin_3, D8.A
  N22: S9.pin_3, D10.A
  N23: S10.pin_3, D11.A
  N24: S11.pin_3, D10_2.A
  N25: S12.pin_3, D14.A
  N26: S13.pin_3, D14_2.A
  N27: S14.pin_3, D15.A
  N28: S15.pin_3, D17.A
  N29: S18.pin_3, D18.A
  N30: S17.pin_3, D16.A
  N31: D1.A, S1.pin_3

notes:
  Num Pad
  v0.1

custom parts:
  Cherry MX Keyswitch: Cherry MX Keyswitch button for keyboards
